# Fritzing sketch Hardware_v1_emitterCircuit (saved by Fritzing 0.9.3b)
breadboards: 1

parts:
  R1 = Resistor [tolerance=±5% resistance=120 package=THT]
  FET1 = MOSFET-NCHANNEL [package=to220v]
  +5V_Ctrl = Voltage Regulator - 5V [package="DPak [SMD]"]
  GND = BANANA_CONN [package=banana_conn]
  Cin = Ceramic Capacitor [capacitance=100nF package="100 mil [THT, multilayer]"]
  Cout = Ceramic Capacitor [capacitance=100nF package="100 mil [THT, multilayer]"]
  ServoCon = Header 3 [package=molex-1x3_lock]
  +24V = BANANA_CONN [package=banana_conn]
  +Motor = Header 2 [package=jst-2-pth-ns]
  -Motor = Header 2 [package=jst-2-pth-ns]
  ARduino = Arduino Nano (Rev3.0) (ICSP)

nets:
  N1: R1.Pin_0, ARduino.D9
  N2: R1.Pin_1, FET1.G
  N3: FET1.D, -Motor.1, -Motor.2
  GND: FET1.S, GND.1, ServoCon.3, ARduino.GND
  24V: +5V_Ctrl.input_voltage, Cin.1, +24V.1, +Motor.1, +Motor.2
  N4: +5V_Ctrl.GND, Cin.0, Cout.0
  5V: +5V_Ctrl.output_voltage, Cout.1, ServoCon.2, ARduino.VIN
  N5: ServoCon.1, ARduino.D2
