# Fritzing sketch Hardware_v2_Fullbridge (saved by Fritzing 0.9.3b)
perfboards: 1

parts:
  R1 = Resistor [tolerance=±5% resistance=120 package=THT]
  H+ = MOSFET-NCHANNEL [package=to220v]
  +5V_Ctrl = Voltage Regulator - 5V [package="DPak [SMD]"]
  GND = BANANA_CONN [package=banana_conn]
  Cin = Ceramic Capacitor [capacitance=100nF package="100 mil [THT, multilayer]"]
  Cout = Ceramic Capacitor [capacitance=100nF package="100 mil [THT, multilayer]"]
  +24V = BANANA_CONN [package=banana_conn]
  ServoCon = Header 3 [package=molex-1x3_lock]
  Arduino = Arduino Nano (Rev3.0)
  +Motor = Header 2 [package=molex-1x2_lock]
  -Motor = Header 2 [package=molex-1x2_lock]
  L+ = MOSFET-NCHANNEL [package=to220v]
  H- = MOSFET-NCHANNEL [package=to220v]
  L- = MOSFET-NCHANNEL [package=to220v]

nets:
  N1: R1.Pin_0, Arduino.D9
  N2: H+.S, +Motor.1, +Motor.2, L+.D
  24V: +5V_Ctrl.input_voltage, Cin.1, +24V.1
  N3: +5V_Ctrl.GND, Cin.0, Cout.0
  5V: +5V_Ctrl.output_voltage, Cout.1, ServoCon.2, Arduino.VIN
  GND: GND.1, ServoCon.3, Arduino.GND
  N4: ServoCon.1, Arduino.D2
  N5: -Motor.1, -Motor.2, H-.S, L-.D
